# Fritzing sketch Sensor diagram (saved by Fritzing 0.9.2b)
breadboards: 1

parts:
  Onderdeel1 = Arduino Pro Mini v13
  Onderdeel2 = NRF24L01
  Onderdeel3 = BH1750
  DHT1 = DHT22 Humidity and Temperature Sensor
  VCC1 = Battery
  C1 = Capacitor Polarized [package=panasonic_c]
  R1 = Resistor [tolerance=±5% resistance=1M package=THT]
  R2 = Resistor [tolerance=±5% resistance=470k package=THT]

nets:
  N1: Onderdeel1.DTR, VCC1.-, R2.Pin_1
  N2: Onderdeel1.A4, Onderdeel3.SCL
  N3: Onderdeel1.A5, Onderdeel3.SDA
  N4: Onderdeel1.RAW, VCC1.+, R1.Pin_0
  GND: Onderdeel1.GND, Onderdeel2.GND, Onderdeel3.GND, Onderdeel3.ADDR, DHT1.GND, C1.+
  VCC: Onderdeel1.VCC, Onderdeel2.VCC, Onderdeel3.VCC, DHT1.VDD, C1.-
  N5: Onderdeel1.A0, R1.Pin_1, R2.Pin_0
  N6: Onderdeel1.D13/SCK, Onderdeel2.SCK
  N7: Onderdeel1.D12/MISO, Onderdeel2.MISO
  N8: Onderdeel1.D11_PWM/MOSI, Onderdeel2.MOSI
  N9: Onderdeel1.D10_PWM/SS, Onderdeel2.CSN
  N10: Onderdeel1.D9_PWM, Onderdeel2.CE
  N11: Onderdeel1.D3_PWM, DHT1.DATA
  N12: Onderdeel1.D2, Onderdeel2.IRQ

custom parts:
  BH1750: Light Sensor
  Battery: Your standard 2x 18650 battery pack (7,4 Volts)
